# Fritzing sketch Schematic RPi Activity 3 (saved by Fritzing 0.9.3b)
breadboards: 1

parts:
  S1 = Pushbutton [package="[THT]"]
  S2 = Pushbutton [package="[THT]"]
  S3 = Pushbutton [package="[THT]"]
  S4 = Pushbutton [package="[THT]"]
  Raspberry_Pi_1 = Raspberry Pi 3 [part_number=RPI-3-V1.2]

nets:
  N1: S1.Pin_1, Raspberry_Pi_1.GPIO23
  N2: S1.Pin_3, S1.Pin_4, S2.Pin_3, S2.Pin_4, S3.Pin_3, S3.Pin_4, S4.Pin_3, Raspberry_Pi_1.3v3
  N3: S2.Pin_1, Raspberry_Pi_1.GPIO18
  N4: S3.Pin_1, Raspberry_Pi_1.GPIO24
  N5: S4.Pin_1, Raspberry_Pi_1.GPIO25
